# Fritzing sketch runebook (saved by Fritzing 0.9.3b)

parts:
  Part1 = Arduino Mega 2560 (Rev3)
  Q7 = PNP-Transistor [package="TO92 [THT]"]
  Q8 = PNP-Transistor [package="TO92 [THT]"]
  Q9 = PNP-Transistor [package="TO92 [THT]"]
  Q13 = PNP-Transistor [package="TO92 [THT]"]
  Q14 = PNP-Transistor [package="TO92 [THT]"]
  Q15 = PNP-Transistor [package="TO92 [THT]"]
  Q16 = PNP-Transistor [package="TO92 [THT]"]
  Q17 = PNP-Transistor [package="TO92 [THT]"]
  Q18 = PNP-Transistor [package="TO92 [THT]"]

nets:
  N1: Part1.A8, Q17.C
  N2: Part1.A0, Q9.C
  N3: Part1.A1, Q7.C
  N4: Part1.A2, Q8.C
  N5: Part1.A3, Q13.C
  N6: Part1.A4, Q15.C
  N7: Part1.A5, Q14.C
  N8: Part1.A6, Q16.C
  N9: Part1.A7, Q18.C
  N10: Part1.GND, Q7.E, Q8.E, Q9.E, Q13.E, Q14.E, Q15.E, Q16.E, Q17.E, Q18.E
  N11: Part1.VIN, Q7.B, Q8.B, Q9.B, Q13.B, Q14.B, Q15.B, Q16.B, Q17.B, Q18.B

notes:
  < 12V
  00
  03
  06
  30
  33
  60
  36
  63
  66
